# Fritzing sketch scarp_clock_filled (saved by Fritzing 1.0.2b)
circuit board: 8.3cm x 9.2cm
breadboards: 2

parts:
  1K = Resistor [tolerance=±5% power=0.25 resistance=1k package=THT]
  J4 = female pin header, 20 pins [form="♀ (female)"]
  Raspberry_Pi_Pico = Raspberry Pi Pico
  10K = Rotary Potentiometer (Small) [maximum_resistance=10kΩ knob_status=50% power=0.5W package=THT]
  10K_2 = Rotary Potentiometer (Small) [maximum_resistance=10kΩ knob_status=50% power=0.5W package=THT]
  LED1 = LED - 3mm [color="Red (633nm)" current=0.030A package="3 mm [THT]"]
  1K_2 = Resistor [tolerance=±5% power=0.25 resistance=1k package=THT]
  LED2 = LED - 3mm [color="Red (633nm)" current=0.030A package="3 mm [THT]"]
  1K_3 = Resistor [tolerance=±5% power=0.25 resistance=1k package=THT]
  LED3 = LED - 3mm [color="Red (633nm)" current=0.030A package="3 mm [THT]"]
  1K_4 = Resistor [tolerance=±5% power=0.25 resistance=1k package=THT]
  LED4 = LED - 3mm [color="Red (633nm)" current=0.030A package="3 mm [THT]"]
  1K_5 = Resistor [tolerance=±5% power=0.25 resistance=1k package=THT]
  LED5 = LED - 3mm [color="Red (633nm)" current=0.030A package="3 mm [THT]"]
  1K_6 = Resistor [tolerance=±5% power=0.25 resistance=1k package=THT]
  LED6 = LED - 3mm [color="Red (633nm)" current=0.030A package="3 mm [THT]"]
  1K_7 = Resistor [tolerance=±5% power=0.25 resistance=1k package=THT]
  LED7 = LED - 3mm [color="Red (633nm)" current=0.030A package="3 mm [THT]"]
  1K_8 = Resistor [tolerance=±5% power=0.25 resistance=1k package=THT]
  LED8 = LED - 3mm [color="Red (633nm)" current=0.030A package="3 mm [THT]"]
  S1 = Pushbutton [package="[THT]"]
  S2 = Pushbutton [package="[THT]"]
  S3 = Pushbutton [package="[THT]"]
  S4 = Pushbutton [package="[THT]"]
  S5 = Pushbutton [package="[THT]"]
  S6 = Pushbutton [package="[THT]"]
  S7 = Pushbutton [package="[THT]"]
  S8 = Pushbutton [package="[THT]"]
  Audio_OUt = Audio Jack (TRS) 3.5mm [package="PG203J [THT]"]
  ClkIn = Audio Jack (TRS) 3.5mm [package="PG203J [THT]"]
  clckaudio = Audio Jack (TRS) 3.5mm [package="PG203J [THT]"]
  10K_3 = Resistor [tolerance=±5% resistance=10k power=0.25W package=THT]
  10k = Resistor [tolerance=±5% resistance=10k power=0.25W package=THT]
  1KΩ = Resistor [tolerance=±5% resistance=1k power=0.25W package=THT]
  J2 = female pin header, 20 pins [form="♀ (female)"]
  oled = OLED 0.96" 128x64 I2C SSD1306
  104 = Capacitor [package=cap-pth-5mm]
  105 = Capacitor [package=cap-pth-5mm]
  100Ω1 = Resistor [tolerance=±5% power=0.25 resistance=100 package=THT]
  10K_4 = Resistor [tolerance=±5% power=0.25 resistance=10k package=THT]
  100Ω2 = Resistor [tolerance=±5% power=0.25 resistance=100 package=THT]
  2N3904 = NPN-Transistor [package="TO92 [THT]"]
  BAT1 = 18650 battery holder [package=battery-18650-kit]
  10K1 = Rotary Potentiometer (Small) [maximum_resistance=10kΩ knob_status=50% power=0.5W package=THT]
  D2 = Rectifier Diode [part_number=1N4001 package="300 mil [THT]"]
  S9 = SPST Switch [package=switch-spdt_kit]  # not connected
  RE3 = Rotary Encoder [package=THT]  # not connected
  J5 = female pin header, 3 pins [form="♀ (female)"]  # not connected
  J6 = female pin header, 6 pins [form="♀ (female)"]  # not connected

nets (from the schematic view):
  N1: 1K.Pin_0, LED1.cathode
  ENC_C/GND: 1K.Pin_1, J4.pin3, J4.pin8, J4.pin18, Raspberry_Pi_Pico.pin_3, Raspberry_Pi_Pico.pin_13, Raspberry_Pi_Pico.pin_18, Raspberry_Pi_Pico.pin_23, Raspberry_Pi_Pico.pin_33, Raspberry_Pi_Pico.pin_38, Raspberry_Pi_Pico.pin_42, 10K.leg2, 10K_2.leg2, 1K_2.Pin_1, 1K_3.Pin_1, 1K_4.Pin_1, 1K_5.Pin_1, 1K_6.Pin_1, 1K_7.Pin_1, 1K_8.Pin_1, Audio_OUt.Sleeve, ClkIn.Sleeve, clckaudio.Sleeve, J2.pin18, oled.VCC, 104.1, 10K_4.Pin_1, 2N3904.E, BAT1.-
  N2: J4.pin1, Raspberry_Pi_Pico.pin_40
  3.3V: J4.pin5, Raspberry_Pi_Pico.pin_36, 10K.leg1, 10K_2.leg1, 10k.Pin_1, oled.GND
  ENC_SW: J4.pin7, Raspberry_Pi_Pico.pin_34
  POT_1: J4.pin9, Raspberry_Pi_Pico.pin_32, 10K.wiper
  POT_2: J4.pin10, Raspberry_Pi_Pico.pin_31, 10K_2.wiper
  N3: J4.pin11, Raspberry_Pi_Pico.pin_30
  N4: J4.pin12, Raspberry_Pi_Pico.pin_29, 105.1
  SCL: J4.pin14, Raspberry_Pi_Pico.pin_27, oled.SCL
  SDA: J4.pin15, Raspberry_Pi_Pico.pin_26, oled.SCA
  ENC_B: J4.pin16, Raspberry_Pi_Pico.pin_25
  ENC_A: J4.pin17, Raspberry_Pi_Pico.pin_24
  CLK_IN: J4.pin19, Raspberry_Pi_Pico.pin_22, 10k.Pin_0, 2N3904.C
  CLK_OUT: J4.pin20, Raspberry_Pi_Pico.pin_21, 1KΩ.Pin_0
  N5: Raspberry_Pi_Pico.pin_1, J2.pin1
  N6: Raspberry_Pi_Pico.pin_2, J2.pin2
  N7: Raspberry_Pi_Pico.pin_4, J2.pin4
  N8: Raspberry_Pi_Pico.pin_5, J2.pin5
  N9: Raspberry_Pi_Pico.pin_6, J2.pin6
  N10: Raspberry_Pi_Pico.pin_7, J2.pin7
  N11: Raspberry_Pi_Pico.pin_9, J2.pin9
  N12: Raspberry_Pi_Pico.pin_10, J2.pin10
  N13: Raspberry_Pi_Pico.pin_11, J2.pin11
  N14: Raspberry_Pi_Pico.pin_12, J2.pin12
  N15: Raspberry_Pi_Pico.pin_14, J2.pin14
  N16: Raspberry_Pi_Pico.pin_15, J2.pin15
  N17: Raspberry_Pi_Pico.pin_16, J2.pin16
  N18: Raspberry_Pi_Pico.pin_17, J2.pin17
  N19: Raspberry_Pi_Pico.pin_19, J2.pin19
  N20: Raspberry_Pi_Pico.pin_20, LED8.anode, J2.pin20
  N21: 1K_2.Pin_0, LED2.cathode
  N22: 1K_3.Pin_0, LED3.cathode
  N23: 1K_4.Pin_0, LED4.cathode
  N24: 1K_5.Pin_0, LED5.cathode
  N25: 1K_6.Pin_0, LED6.cathode
  N26: 1K_7.Pin_0, LED7.cathode
  N27: 1K_8.Pin_0, LED8.cathode
  N28: S1.Pin_1, S1.Pin_2
  N29: S1.Pin_3, S1.Pin_4, S2.Pin_3, S2.Pin_4, S3.Pin_3, S3.Pin_4, S4.Pin_3, S4.Pin_4, S5.Pin_3, S5.Pin_4, S6.Pin_3, S6.Pin_4
  N30: S2.Pin_1, S2.Pin_2
  N31: S3.Pin_1, S3.Pin_2
  N32: S4.Pin_1, S4.Pin_2
  N33: S5.Pin_1, S5.Pin_2
  N34: S6.Pin_1, S6.Pin_2
  N35: S7.Pin_1, S7.Pin_2
  N36: S7.Pin_3, S7.Pin_4, S8.Pin_3, S8.Pin_4
  N37: S8.Pin_1, S8.Pin_2
  AUDIO: Audio_OUt.Ring, Audio_OUt.Tip, ClkIn.Ring, clckaudio.Ring, 100Ω2.Pin_0
  N38: ClkIn.Tip, 10K_3.Pin_0
  N39: clckaudio.Tip, 1KΩ.Pin_1
  N40: 10K_3.Pin_1, 2N3904.B
  N41: 104.2, 100Ω2.Pin_1, 10K1.leg2
  N42: 105.2, 100Ω1.Pin_1, 10K_4.Pin_0
  N43: 100Ω1.Pin_0, 10K1.wiper
  N44: BAT1.+, D2.anode

notes:
  scarp v1.0.2
  scarp (2024-02-06)
  Made with fritzing
  USB
  blueprint@poetaster.de 2024

custom parts:
  Raspberry Pi Pico: Raspberry Pi Pico. Based around the RP2040 microcontroller the Pico is a low cost microcontroller device bringing Raspberry Pi quality, cost, and easy of use to the microcontroller space. Jan 2021, Split part in to two versions: tht (this one) and SMD. This one will drill holes for a .1 in header in pcb to allow plugging in the module as well as providing pads to solder the module to the top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
  18650 battery holder: 18650 Battery Holder
  Rotary Encoder: Rotary Encoder with push button

// code stored in the sketch: EasyPicoPCB.ino

